# Fritzing sketch buttonInput (saved by Fritzing 0.9.3b)
breadboards: 1

parts:
  LED1 = LED - 5mm [color="Blue (470nm)" package="5 mm [THT]"]
  R1 = Resistor [tolerance=±5% resistance=1k package=THT]
  S1 = Pushbutton [package="[THT]"]
  Part1 = Adafruit HUZZAH32 ESP32 Feather [part_number="Adafruit #3405"]

nets:
  N1: LED1.cathode, R1.Pin_0
  N2: LED1.anode, Part1.IO27_A10
  N3: R1.Pin_1, S1.Pin_1, S1.Pin_2, Part1.GND
  N4: S1.Pin_3, S1.Pin_4, Part1.IO15_A8

// code stored in the sketch: 01-pwmLED.ino

