# Fritzing sketch oneLED (saved by Fritzing 0.9.3b)
breadboards: 1

parts:
  LED1 = LED - 5mm [color="Blue (430nm)" package="5 mm [THT]"]
  R1 = Resistor [tolerance=±5% resistance=1k package=THT]
  Part2 = Adafruit HUZZAH32 ESP32 Feather [part_number="Adafruit #3405"]

nets:
  N1: LED1.cathode, R1.Pin_1
  N2: LED1.anode, Part2.IO27_A10
  N3: R1.Pin_0, Part2.GND
