# Fritzing sketch subway_wiring (saved by Fritzing 0.9.3b)
breadboards: 1

parts:
  Part1 = Adafruit HUZZAH32 ESP32 Feather [part_number="Adafruit #3405"]
  U2 = LCD-16X2 [package=lcd-16x2]

nets:
  GND: Part1.GND, U2.VSS
  N1: Part1.VBUS, U2.VDD
  N2: Part1.IO13_A12, U2.DB7
  N3: Part1.IO12_A11, U2.DB6
  N4: Part1.IO27_A10, U2.DB5
  N5: Part1.IO33_A9, U2.DB4
  N6: Part1.IO15_A8, U2.E
  N7: Part1.IO32_A7, U2.R_W
  N8: Part1.IO14_A6, U2.RS
